# Fritzing sketch catdoor_shield (saved by Fritzing 0.9.3b)
circuit board: 6.2cm x 2.7cm
breadboards: 1

parts:
  Q1 = MOSFET-NCHANNEL [package=to220v]
  Q2 = MOSFET-NCHANNEL [package=to220v]
  LED1 = LED - 3mm [color="Red (633nm)" package="3 mm [THT]"]
  LED2 = LED - 3mm [color="Red (633nm)" package="3 mm [THT]"]
  R1 = Resistor [tolerance=±5% resistance=1k package=THT]
  R2 = Resistor [tolerance=±5% resistance=1k package=THT]
  D1 = Rectifier Diode [part_number=1N4001 package="300 mil [THT]"]
  D2 = Rectifier Diode [part_number=1N4001 package="300 mil [THT]"]
  IN-5V = Power Jack [package=power_jack_pth_lock]
  JP-SOLE = Header 3 [package=screwterminal-3.5mm-3_lock.007s]
  Q3 = TRANSISTOR_NPN [package=to-92-ammo]
  R3 = Resistor [tolerance=±5% resistance=220 package=THT]
  R4 = Resistor [tolerance=±5% resistance=1k package=THT]
  LED3 = LED - 3mm [color="Yellow (595nm)" package="3 mm [THT]"]
  Part5 = Adafruit Feather M0 WINC1500 [part_number="Adafruit #3010"]
  JP-AUX = Header 4 [package=molex-1x4_lock]
  JP-I2C = Header 4 [package=molex-1x4_lock]
  JP-PWR = Header 4 [package=molex-1x4_lock]

nets:
  N1: Q1.G, LED1.anode, Part5.D5
  N2: Q1.D, D1.anode, JP-SOLE.2
  GND: Q1.S, Q2.S, R1.Pin_1, R2.Pin_1, IN-5V.GND, IN-5V.GNDBREAK, Q3.E, Part5.GND, JP-AUX.2, JP-PWR.2, JP-PWR.4
  N3: Q2.G, LED2.anode, Part5.D6
  N4: Q2.D, D2.anode, JP-SOLE.3
  N5: LED1.cathode, R1.Pin_0
  N6: LED2.cathode, R2.Pin_0
  N7: D1.cathode, D2.cathode, IN-5V.PWR, JP-SOLE.1, R3.Pin_0, Part5.VBUS
  N8: Q3.B, R4.Pin_1
  N9: Q3.C, LED3.cathode
  N10: R3.Pin_1, LED3.anode
  N11: R4.Pin_0, Part5.D11
  N12: Part5.A2, JP-AUX.4
  N13: Part5.A1, JP-AUX.3
  N14: Part5.+3V3, JP-AUX.1, JP-PWR.1, JP-PWR.3
  N15: Part5.SCL, JP-I2C.1, JP-I2C.3
  N16: Part5.SDA, JP-I2C.2, JP-I2C.4

custom parts:
  Adafruit Feather M0 WINC1500: This is the Adafruit Feather M0 WiFi w/ATWINC1500 - our take on an 'all-in-one' Arduino-compatible + high speed, reliable WiFi with built in USB and battery charging. Its an Adafruit Feather M0 with a WiFi module, ready to rock! Connect your Feather to the Internet with this fine new FCC-certified WiFi module from Atmel. This 802.11bgn-capable WiFi module is the best new thing for networking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
